# Fritzing sketch devre (saved by Fritzing 1.0.0d)
breadboards: 1

parts:
  Mod7 = 2S-BMS
  M7 = tp5100 [package=THT]
  U9 = ESP8266 NodeMCU LoLin module
  Bat7 = battery_holder_single_18650
  Bat8 = battery_holder_single_18650
  MOD7 = MT3608 Boost No usb
  MOD8 = MT3608 Boost No usb
  buz4 = Piezo Buzzer
  Mod8 = sensor_biometrico
  SIM800L4 = SIM800L
  microSD4 = MicroSD Card Module
  Part8 = Arduino Uno (Rev3) - ICSP
  LCD1 = LCD screen
  IC1 = L293D [package=THT]
  LLC1 = Logic Level Converter [package="Breakout board"]
  M10 = DC Motor [voltage_(max)=6V voltage_(min)=3V]
  R1 = Resistor [tolerance=±5% resistance=1k package="2512 [SMD]"]
  R4 = Resistor [tolerance=±5% resistance=220 package="0402 [SMD]"]

nets:
  N1: Mod7.pin1, Bat8.+#1
  GND: Mod7.pin2, U9.GND, Bat7.+#0, MOD8.IN_(-), MOD8.OUT_(-), microSD4.GND, IC1.0V, IC1.In_2, LLC1.H-GND
  N2: Mod7.pin3#2, M7.-IN, M7.-BAT, MOD7.OUT_(-)
  N3: Mod7.pin3#3, M7.+BAT, U9.Vin, MOD8.IN_(+)
  N4: Mod7.pin3#4, Bat7.+#1, Bat8.+#0
  N5: M7.+_IN, MOD7.OUT_(+)
  N6: U9.D0, LLC1.LV1
  N7: U9.D1, Part8.D2
  N8: U9.D4, LLC1.LV4
  3V3: U9.3V3, microSD4.VCC
  N9: U9.D5, microSD4.SCK
  N10: U9.D6, microSD4.MISO
  N11: U9.D7, microSD4.MOSI
  N12: U9.D8, microSD4.CS
  N13: U9.RX, Mod8.RX
  N14: U9.TX, Mod8.TX
  N15: MOD8.OUT_(+), IC1.+Vmotor
  GND_2: buz4.pin_1, Mod8.GND, Part8.GND, LCD1.VSS, LCD1.R/W, LCD1.LED-
  N16: buz4.pin_2, Part8.D5_PWM
  VCC: Mod8.VCC, SIM800L4.VCC, Part8.3V3, LLC1.LV
  N17: SIM800L4.RXD, Part8.D13/SCK
  N18: SIM800L4.TXD, Part8.D12/MISO
  N19: SIM800L4.GND, LLC1.L-GND, R4.Pin_0
  N20: Part8.D8, LCD1.DB3, LCD1.DB4
  N21: Part8.D9_PWM, LCD1.DB5
  N22: Part8.D10_PWM/SS, LCD1.DB6
  N23: Part8.D11_PWM/MOSI, LCD1.DB7
  N24: Part8.D3_PWM, LLC1.HV1
  N25: Part8.D6_PWM, LCD1.RS
  N26: Part8.D7, LCD1.E
  5V: Part8.5V, LCD1.VDD, LCD1.LED+, IC1.Enable_1, IC1.+V, LLC1.HV, R1.Pin_0
  N27: LCD1.V0, R1.Pin_1, R4.Pin_1
  N28: IC1.In_1, LLC1.HV4
  N29: IC1.Out_1_(_Controlled_by_Enable_1_), M10.pin_2
  N30: IC1.Out_2_(_Controlled_by_Enable_1_), M10.pin_1

custom parts:
  2S-BMS: 2S-BMS LIPO battery charger / protection unit. Note pcb does not match the board as it will likely connect with wires, so pcb is 5 pads suitable for .1in header pins.
  tp5100: Tp5100 battery charger module. Generic ebay type.
  ESP8266 NodeMCU LoLin module: ESP8266 based NodeMCU
  battery_holder_single_18650: single 18650 battery holder
  MT3608 Boost No usb: Chip- MT3608 / B6289 DC to DC step up, power booster module. With adjustable output voltage. Current- 2A . || Input voltage- 2V-24V || Output voltage- 5V-28V Input interface- Inversed polarity- NO. || Led indicator- No.
  Piezo Buzzer: Part from https://www.nutsvolts.com/magazine/article/november2012_SmileysWorkshop. Breadboard and icon images modified to be 0.3" in spacing and be more similar to the actual physical part.
  sensor_biometrico: Adafruit Optical Fingerprint Sensor
  SIM800L: SIM800L is a miniature cellular module which allows for GPRS transmission, sending and receiving SMS and making and receiving voice calls. Low cost and small footprint and quad band frequency support make this module perfect solution for any project that require long range connectivity. After connecting power module boots up, searches for cellular network and login automatically. On board LED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
  Logic Level Converter: 5V to/from 3.3V logic level converter
